# Fritzing sketch Project1A (saved by Fritzing 0.8.0b)
breadboards: 1

parts:
  LED1 = LED - 5mm [color="Red (633nm)" package="5 mm [THT]"]
  Part1 = Arduino Uno (Rev3)

nets:
  N1: LED1.cathode, Part1.D12/MISO
  N2: LED1.anode, Part1.GND
