# Fritzing sketch Project2 (saved by Fritzing 0.8.7b)
breadboards: 1

parts:
  S1 = Pushbutton [package="[THT]"]
  R1 = Resistor [tolerance=±5% resistance=1k package=THT]
  LED1 = LED - 5mm [color="Red (633nm)" package="5 mm [THT]"]
  Part1 = Arduino Uno (Rev3)

nets:
  N1: S1.Pin_1, S1.Pin_2, R1.Pin_0, LED1.cathode
  N2: S1.Pin_3, S1.Pin_4, LED1.anode, Part1.5V
  N3: R1.Pin_1, Part1.GND
