# Fritzing sketch Project4 (saved by Fritzing 0.8.0b)
breadboards: 1

parts:
  Part1 = Arduino Uno (Rev3)
  S1 = Pushbutton [package="[THT]"]
  R1 = Resistor [tolerance=±5% resistance=1k package=THT]
  LED1 = LED - 5mm [color="Red (633nm)" package="5 mm [THT]"]

nets:
  N1: Part1.ICSP_MOSI, Part1.D11_PWM/MOSI, LED1.anode
  N2: Part1.GND, LED1.cathode
  N3: Part1.D2, S1.Pin_1, S1.Pin_2, R1.Pin_0
  N4: Part1.5V, S1.Pin_3, S1.Pin_4, R1.Pin_1

notes:
  D2
  D11
